// Logisim project flipflooop.circ as structural Verilog: 1 circuit, main circuit main
module main (
  output out_1
);

  wire _1_out, _2_out, _3_out, _4_out, _5_out, _6_out, _7_out, _8_out, _9_out, _10_out, _11_out, _12_out,
       _13_out, and_1_out, clock_1_out, d_ff_1_q, d_ff_1_qn, d_ff_2_q, d_ff_2_qn, d_ff_3_q, d_ff_3_qn,
       d_ff_4_q, d_ff_4_qn, not_1_out, not_2_out, not_3_out, not_4_out, or_1_out, or_2_out, or_3_out,
       or_4_out, or_5_out, undriven;

  and _0 (out_1, not_1_out, not_2_out, not_3_out, not_4_out);
  Clock clock_1 (.out(clock_1_out));
  or or_1 (or_1_out, _13_out, _11_out, _10_out, _9_out);
  and _1 (_1_out, d_ff_1_q, not_2_out, not_3_out, not_4_out);
  and _2 (_2_out, not_1_out, d_ff_2_q, not_3_out, not_4_out);
  and _3 (_3_out, d_ff_1_q, d_ff_2_q, not_3_out, not_4_out);
  not not_1 (not_1_out, d_ff_1_q);
  D_Flip_Flop d_ff_1 (.clk(clock_1_out), .D(d_ff_1_qn), .Q(d_ff_1_q), .Qn(d_ff_1_qn));  // open: preset, en, reset
  LED led_1 (.in(or_1_out));
  LED led_2 (.in(or_1_out));
  or or_2 (or_2_out, _13_out, _11_out, _8_out, _7_out);
  and _5 (_5_out, d_ff_1_q, not_2_out, d_ff_3_q, not_4_out, undriven);
  and _4 (_4_out, not_1_out, not_2_out, d_ff_3_q, not_4_out);
  not not_2 (not_2_out, d_ff_2_q);
  and and_1 (and_1_out, d_ff_1_q, not_2_out, d_ff_3_q, d_ff_4_q);
  LED led_3 (.in(or_1_out));
  LED led_4 (.in(or_1_out));
  LED led_5 (.in(or_2_out));
  LED led_6 (.in(or_2_out));
  or or_3 (or_3_out, _5_out, _13_out, _11_out, _6_out);
  and _6 (_6_out, undriven, not_1_out, d_ff_2_q, not_4_out, d_ff_1_q);
  D_Flip_Flop d_ff_2 (.clk(d_ff_1_qn), .D(d_ff_2_qn), .Q(d_ff_2_q), .Qn(d_ff_2_qn));  // open: preset, en, reset
  LED led_7 (.in(or_1_out));
  LED led_8 (.in(or_1_out));
  LED led_9 (.in(or_2_out));
  LED led_10 (.in(or_1_out));
  LED led_11 (.in(or_2_out));
  LED led_12 (.in(or_2_out));
  LED led_13 (.in(or_3_out));
  LED led_14 (.in(or_3_out));
  LED led_15 (.in(or_3_out));
  LED led_16 (.in(or_4_out));
  LED led_17 (.in(or_4_out));
  LED led_18 (.in(or_5_out));
  LED led_19 (.in(or_5_out));
  LED led_20 (.in(or_5_out));
  LED led_21 (.in(or_5_out));
  or or_4 (or_4_out, _13_out, _3_out, _4_out, _11_out);
  and _7 (_7_out, d_ff_1_q, d_ff_2_q, d_ff_3_q, not_4_out);
  and _8 (_8_out, not_1_out, not_2_out, not_3_out, d_ff_4_q);
  not not_3 (not_3_out, d_ff_3_q);
  LED led_22 (.in(or_1_out));
  LED led_23 (.in(or_1_out));
  LED led_24 (.in(or_1_out));
  LED led_25 (.in(or_2_out));
  LED led_26 (.in(or_2_out));
  LED led_27 (.in(or_2_out));
  LED led_28 (.in(or_3_out));
  LED led_29 (.in(or_3_out));
  LED led_30 (.in(or_3_out));
  LED led_31 (.in(or_4_out));
  LED led_32 (.in(or_4_out));
  LED led_33 (.in(or_4_out));
  LED led_34 (.in(or_5_out));
  LED led_35 (.in(or_5_out));
  LED led_36 (.in(or_5_out));
  LED led_37 (.in(or_5_out));
  LED led_38 (.in(or_5_out));
  and _9 (_9_out, d_ff_1_q, not_2_out, not_3_out, d_ff_4_q);
  and _10 (_10_out, not_1_out, d_ff_2_q, not_3_out, d_ff_4_q);
  not not_4 (not_4_out, d_ff_4_q);
  D_Flip_Flop d_ff_3 (.clk(d_ff_2_qn), .D(d_ff_3_qn), .Q(d_ff_3_q), .Qn(d_ff_3_qn));  // open: preset, en, reset
  LED led_39 (.in(or_1_out));
  LED led_40 (.in(or_1_out));
  LED led_41 (.in(or_1_out));
  LED led_42 (.in(or_2_out));
  LED led_43 (.in(or_2_out));
  LED led_44 (.in(or_3_out));
  and _11 (_11_out, d_ff_1_q, d_ff_2_q, not_3_out, d_ff_4_q);
  LED led_45 (.in(or_1_out));
  LED led_46 (.in(or_1_out));
  LED led_47 (.in(or_2_out));
  and _12 (_12_out, not_1_out, not_2_out, d_ff_3_q, d_ff_4_q);
  and _13 (_13_out, d_ff_1_q, not_2_out, d_ff_3_q, d_ff_4_q);
  or or_5 (or_5_out, _1_out, _2_out, _3_out, _4_out, _5_out, _6_out, _7_out, _8_out, _9_out, _10_out, _11_out, _13_out);
  // AND_Gate Disabled is placed but not wired
  // AND_Gate Disabled_2 is placed but not wired
  D_Flip_Flop d_ff_4 (.clk(d_ff_3_qn), .D(d_ff_4_qn), .Q(d_ff_4_q), .Qn(d_ff_4_qn));  // open: preset, en, reset
endmodule
